# Fritzing sketch sensor kotelna (saved by Fritzing 0.9.3b)
breadboards: 1

parts:
  UNO = Arduino Uno (Rev3)
  U1 = MAX6675 [package=so08]
  DS3 = DS18B20 1-Wire Temperature Sensor [part_number=DS18B20]
  DS5 = DS18B20 1-Wire Temperature Sensor [part_number=DS18B20]
  DS6 = DS18B20 1-Wire Temperature Sensor [part_number=DS18B20]
  IC1 = Voltage Regulator AMS1117 [package=sot223]
  Součástka1 = NRF24L01
  R1 = Resistor [tolerance=±5% resistance=4.7k package="2010 [SMD]"]
  OLED1 = OLED 128x64 I2C Monochrome Display

nets:
  N1: UNO.A4/SDA, OLED1.SCK
  N2: UNO.A5/SCL, OLED1.SDA
  N3: UNO.D8, U1.SCK
  N4: UNO.D9_PWM, Součástka1.CE
  N5: UNO.D10_PWM/SS, Součástka1.CSN
  N6: UNO.D11_PWM/MOSI, Součástka1.MOSI
  N7: UNO.D12/MISO, U1.MISO, Součástka1.MISO
  N8: UNO.D13/SCK, Součástka1.SCK
  N9: UNO.D2, DS3.DQ, DS5.DQ, DS6.DQ, R1.Pin_1, OLED1.GND
  N10: UNO.D7, U1.CS
  N11: UNO.5V, IC1.IN
  GND: UNO.GND, U1.VSS, DS3.GND, DS5.GND, DS6.GND, IC1.GND, Součástka1.GND
  N12: U1.VDD, IC1.OUT
  VDD: DS3.VDD, DS5.VDD, DS6.VDD, Součástka1.VCC, R1.Pin_0, OLED1.VDD
