# Fritzing sketch senzor kotelna (saved by Fritzing 0.9.3b)
breadboards: 1

parts:
  UNO = Arduino Uno (Rev3)
  U1 = MAX6675 [package=so08]
  DS3 = DS18B20 1-Wire Temperature Sensor [part_number=DS18B20]
  DS5 = DS18B20 1-Wire Temperature Sensor [part_number=DS18B20]
  DS6 = DS18B20 1-Wire Temperature Sensor [part_number=DS18B20]
  IC1 = Voltage Regulator AMS1117 [package=sot223]
  Součástka1 = NRF24L01
  R1 = Resistor [tolerance=±5% resistance=4.7k package="2010 [SMD]"]

nets:
  N1: UNO.D8, U1.SCK
  N2: UNO.D9_PWM, Součástka1.CE
  N3: UNO.D10_PWM/SS, Součástka1.CSN
  N4: UNO.D11_PWM/MOSI, Součástka1.MOSI
  N5: UNO.D12/MISO, U1.MISO, Součástka1.MISO
  N6: UNO.D13/SCK, Součástka1.SCK
  VDD: UNO.D2, DS3.VDD, DS5.VDD, DS6.VDD, Součástka1.VCC, R1.Pin_0
  N7: UNO.D7, U1.CS
  N8: UNO.5V, IC1.IN
  GND: UNO.GND, U1.VSS, DS3.GND, DS5.GND, DS6.GND, IC1.GND, Součástka1.GND
  N9: U1.VDD, IC1.OUT
  N10: DS3.DQ, DS5.DQ, DS6.DQ, R1.Pin_1
